// Logisim project 1. flip-flop_JK_D.circ as structural Verilog
module flipflop_jk (
  input  Reset,
  input  J,
  input  K,
  input  clear,
  output Q,
  output nQ
);

  wire clock_1_out, nand_1_out, nand_2_out, nand_3_out, nand_4_out, nand_5_out, nand_6_out, not_1_out,
       not_2_out, not_3_out;

  Clock clock_1 (.out(clock_1_out));
  not not_1 (not_1_out, Reset);
  nand nand_1 (nand_1_out, nQ, J, clock_1_out);
  not not_2 (not_2_out, clock_1_out);
  nand nand_2 (nand_2_out, clock_1_out, K, Q);
  not not_3 (not_3_out, clear);
  nand nand_3 (nand_3_out, not_1_out, nand_1_out, nand_4_out);
  nand nand_4 (nand_4_out, nand_3_out, nand_2_out, not_3_out);
  nand nand_5 (nand_5_out, nand_3_out, not_2_out);
  nand nand_6 (nand_6_out, not_2_out, nand_4_out);
  nand nand_7 (Q, nand_5_out, nQ);
  nand nand_8 (nQ, Q, nand_6_out);
endmodule

module flipflop_D (
  input  D,
  output Q,
  output nQ
);

  wire clock_1_out, nand_1_out, nand_2_out, not_1_out;

  Clock clock_1 (.out(clock_1_out));
  not not_1 (not_1_out, D);
  nand nand_1 (nand_1_out, D, clock_1_out);
  nand nand_2 (nand_2_out, not_1_out, clock_1_out);
  nor nor_1 (Q, nand_1_out, nQ);
  nor nor_2 (nQ, Q, nand_2_out);

  // Notes on the sheet:
  //   CLK
endmodule
