// Logisim project 3. PORTA_XOR_USANDO_AND_OR_NOT.circ as structural Verilog
module Componente_3 (
  input  A,
  input  B,
  output S
);

  wire and_1_out, and_2_out, not_1_out, not_2_out;

  not not_1 (not_1_out, A);
  not not_2 (not_2_out, B);
  and and_1 (and_1_out, not_1_out, B);
  and and_2 (and_2_out, A, not_2_out);
  or or_1 (S, and_1_out, and_2_out);

  // Notes on the sheet:
  //   S = A' B
  //   S = AB'
  //   S = A'B + AB'
endmodule
