// Logisim project 4.somador 8 bits+Constante 4.circ as structural Verilog: 2 circuits, main circuit Somador de 8 bits
module Somador_de_8_bits (
  input  [7:0] in_1,
  output [7:0] SOMA,
  output out_3
);

  wire full_adder_1_carry_out, full_adder_2_carry_out, full_adder_3_carry_out, full_adder_4_carry_out,
       full_adder_5_carry_out, full_adder_6_carry_out, full_adder_7_carry_out;

  FULL_ADDER full_adder_1 (.A(in_1[0]), .B(1'b0), .carry_in(1'b0), .S(SOMA[0]), .carry_out(full_adder_1_carry_out));
  FULL_ADDER full_adder_2 (
    .A(in_1[1]), .B(1'b0), .carry_in(full_adder_1_carry_out), .S(SOMA[1]), .carry_out(full_adder_2_carry_out));
  FULL_ADDER full_adder_3 (
    .A(in_1[2]), .B(1'b1), .carry_in(full_adder_2_carry_out), .S(SOMA[2]), .carry_out(full_adder_3_carry_out));
  FULL_ADDER full_adder_4 (
    .A(in_1[3]), .B(1'b0), .carry_in(full_adder_3_carry_out), .S(SOMA[3]), .carry_out(full_adder_4_carry_out));
  FULL_ADDER full_adder_5 (
    .A(in_1[4]), .B(1'b0), .carry_in(full_adder_4_carry_out), .S(SOMA[4]), .carry_out(full_adder_5_carry_out));
  FULL_ADDER full_adder_6 (
    .A(in_1[5]), .B(1'b0), .carry_in(full_adder_5_carry_out), .S(SOMA[5]), .carry_out(full_adder_6_carry_out));
  FULL_ADDER full_adder_7 (
    .A(in_1[6]), .B(1'b0), .carry_in(full_adder_6_carry_out), .S(SOMA[6]), .carry_out(full_adder_7_carry_out));
  FULL_ADDER full_adder_8 (.A(in_1[7]), .B(1'b0), .carry_in(full_adder_7_carry_out), .S(SOMA[7]), .carry_out(out_3));

  // Notes on the sheet:
  //   CONSTANTE 4 (EM BINÁRIO)
  //   SOMADOR - 8 BITS
endmodule

module FULL_ADDER (
  input  A,
  input  B,
  input  carry_in,
  output S,
  output carry_out
);

  wire and_1_out, and_2_out, and_3_out, xor_1_out;

  xor xor_1 (xor_1_out, A, B);
  and and_1 (and_1_out, A, B);
  and and_2 (and_2_out, A, carry_in);
  and and_3 (and_3_out, B, carry_in);
  xor xor_2 (S, xor_1_out, carry_in);
  or or_1 (carry_out, and_1_out, and_2_out, and_3_out);
endmodule
