// Logisim project 5memoria-ROM-8 bits.circ as structural Verilog
module ROM_8bits (
  input  A,
  input  B,
  input  C,
  output [7:0] out_4
);

  wire A_prime_B_prime_C_out, A_prime_B_prime_C_prime_out, A_prime_BC_out, A_prime_BC_prime_out,
       AB_prime_C_out, AB_prime_C_prime_out, ABC_out, ABC_prime_out, not_1_out, not_2_out, not_3_out,
       not_4_out, not_5_out, not_6_out, not_7_out, not_8_out, not_9_out, not_10_out, not_11_out, not_12_out;

  not not_1 (not_1_out, A);
  and A_prime_B_prime_C (A_prime_B_prime_C_out, not_4_out, not_3_out, C);
  and A_prime_B_prime_C_prime (A_prime_B_prime_C_prime_out, not_1_out, not_2_out, not_5_out);
  not not_2 (not_2_out, B);
  not not_3 (not_3_out, B);
  not not_4 (not_4_out, A);
  not not_5 (not_5_out, C);
  and A_prime_BC_prime (A_prime_BC_prime_out, not_6_out, B, not_7_out);
  not not_6 (not_6_out, A);
  and A_prime_BC (A_prime_BC_out, not_8_out, B, C);
  not not_7 (not_7_out, C);
  not not_8 (not_8_out, A);
  and AB_prime_C_prime (AB_prime_C_prime_out, A, not_10_out, not_9_out);
  not not_9 (not_9_out, C);
  not not_10 (not_10_out, B);
  and AB_prime_C (AB_prime_C_out, A, not_11_out, C);
  not not_11 (not_11_out, B);
  and ABC_prime (ABC_prime_out, A, B, not_12_out);
  not not_12 (not_12_out, C);
  and ABC (ABC_out, C, B, A);
  or or_1 (out_4[7], AB_prime_C_prime_out, A_prime_BC_prime_out, A_prime_B_prime_C_out, A_prime_B_prime_C_prime_out);
  or or_2 (out_4[6], ABC_prime_out, AB_prime_C_out, A_prime_BC_prime_out, A_prime_B_prime_C_prime_out);
  or or_3 (out_4[5], ABC_out, AB_prime_C_out, A_prime_BC_prime_out, A_prime_B_prime_C_out);
  or or_4 (out_4[4], ABC_out, ABC_prime_out, AB_prime_C_prime_out, A_prime_BC_prime_out);
  or or_5 (out_4[3], AB_prime_C_prime_out, A_prime_BC_out, A_prime_B_prime_C_out, A_prime_B_prime_C_prime_out);
  or or_6 (out_4[2], ABC_prime_out, AB_prime_C_out, A_prime_BC_out, A_prime_B_prime_C_prime_out);
  or or_7 (out_4[1], ABC_out, AB_prime_C_out, A_prime_BC_out, A_prime_B_prime_C_out);
  or or_8 (out_4[0], ABC_out, ABC_prime_out, AB_prime_C_prime_out, A_prime_BC_out);

  // Notes on the sheet:
  //   ENDEREÇO
  //   000
  //   001
  //   010
  //   011
  //   100
  //   101
  //   110
  //   111
  //   SAÍDA
  //   11001100
  //   10101010
  //   11110000
  //   00001111
  //   10011001
  //   01100110
  //   01010101
  //   00110011
endmodule
