// Logisim project 6. Memória RAM 8 Bits (1).circ as structural Verilog: 7 circuits, main circuit Memória RAM de 8 bits
module \Memória_RAM_de_8_bits  (
  input  in_1,
  input  in_2,
  input  in_3,
  input  Set,
  input  [7:0] I,
  input  [2:0] in_6,
  input  Set_2,
  output [7:0] LEITURA
);

  wire A_prime_B_prime_C_out, A_prime_B_prime_C_prime_out, A_prime_BC_out, A_prime_BC_prime_out,
       AB_prime_C_out, AB_prime_C_prime_out, ABC_out, ABC_prime_out, and_1_out, and_2_out, and_3_out,
       and_4_out, and_5_out, and_6_out, and_7_out, and_8_out, not_1_out, not_2_out, not_3_out, not_4_out,
       not_5_out, not_6_out, not_7_out, not_8_out, not_9_out, not_10_out, not_11_out, not_12_out;
  wire [7:0] registrador_de_8_bits_1_s, registrador_de_8_bits_2_s, registrador_de_8_bits_3_s,
       registrador_de_8_bits_4_s, registrador_de_8_bits_5_s, registrador_de_8_bits_6_s,
       registrador_de_8_bits_7_s, registrador_de_8_bits_8_s;

  not not_1 (not_1_out, in_2);
  not not_2 (not_2_out, in_1);
  not not_3 (not_3_out, in_3);
  and A_prime_B_prime_C_prime (A_prime_B_prime_C_prime_out, not_2_out, not_1_out, not_3_out);
  and and_1 (and_1_out, A_prime_B_prime_C_prime_out, Set);
  Registrador_de_8_bits registrador_de_8_bits_1 (.I(I), .CLK(and_1_out), .S(registrador_de_8_bits_1_s));
  not not_4 (not_4_out, in_2);
  not not_5 (not_5_out, in_1);
  and A_prime_B_prime_C (A_prime_B_prime_C_out, not_5_out, not_4_out, in_3);
  and and_2 (and_2_out, A_prime_B_prime_C_out, Set);
  Registrador_de_8_bits registrador_de_8_bits_2 (.I(I), .CLK(and_2_out), .S(registrador_de_8_bits_2_s));
  not not_6 (not_6_out, in_3);
  not not_7 (not_7_out, in_1);
  and A_prime_BC_prime (A_prime_BC_prime_out, not_7_out, in_2, not_6_out);
  and and_3 (and_3_out, A_prime_BC_prime_out, Set);
  Registrador_de_8_bits registrador_de_8_bits_3 (.I(I), .CLK(and_3_out), .S(registrador_de_8_bits_3_s));
  not not_8 (not_8_out, in_1);
  and A_prime_BC (A_prime_BC_out, not_8_out, in_2, in_3);
  and and_4 (and_4_out, A_prime_BC_out, Set);
  Registrador_de_8_bits registrador_de_8_bits_4 (.I(I), .CLK(and_4_out), .S(registrador_de_8_bits_4_s));
  Multiplexador_8x1_8_bits multiplexador_8x1_8_bits_1 (
    .in0(registrador_de_8_bits_1_s), .in1(registrador_de_8_bits_2_s), .in2(registrador_de_8_bits_3_s),
    .in4(registrador_de_8_bits_4_s), .in4_2(registrador_de_8_bits_5_s), .in5(registrador_de_8_bits_6_s),
    .in6(registrador_de_8_bits_7_s), .in7(registrador_de_8_bits_8_s), .chave(in_6), .saida(LEITURA), .S(Set_2));
  not not_9 (not_9_out, in_3);
  not not_10 (not_10_out, in_2);
  and AB_prime_C_prime (AB_prime_C_prime_out, in_1, not_10_out, not_9_out);
  and and_5 (and_5_out, AB_prime_C_prime_out, Set);
  Registrador_de_8_bits registrador_de_8_bits_5 (.I(I), .CLK(and_5_out), .S(registrador_de_8_bits_5_s));
  not not_11 (not_11_out, in_2);
  and AB_prime_C (AB_prime_C_out, in_1, not_11_out, in_3);
  and and_6 (and_6_out, AB_prime_C_out, Set);
  Registrador_de_8_bits registrador_de_8_bits_6 (.I(I), .CLK(and_6_out), .S(registrador_de_8_bits_6_s));
  not not_12 (not_12_out, in_3);
  and ABC_prime (ABC_prime_out, in_1, in_2, not_12_out);
  and and_7 (and_7_out, ABC_prime_out, Set);
  Registrador_de_8_bits registrador_de_8_bits_7 (.I(I), .CLK(and_7_out), .S(registrador_de_8_bits_7_s));
  and ABC (ABC_out, in_3, in_2, in_1);
  and and_8 (and_8_out, ABC_out, Set);
  Registrador_de_8_bits registrador_de_8_bits_8 (.I(I), .CLK(and_8_out), .S(registrador_de_8_bits_8_s));

  // Notes on the sheet:
  //   ESCRITA
  //   Memória RAM de 8 bits
  //   DECODIFICADOR DE ENDEREÇOS
endmodule

module Flip_flop_tipo_D (
  input  D,
  input  CLK,
  output Q,
  output Q_prime
);

  wire nand_1_out, nand_2_out, not_1_out;

  not not_1 (not_1_out, D);
  nand nand_1 (nand_1_out, D, CLK);
  nand nand_2 (nand_2_out, not_1_out, CLK);
  nand nand_3 (Q, nand_1_out, Q_prime);
  nand nand_4 (Q_prime, Q, nand_2_out);

  // Notes on the sheet:
  //   Flip-flop do tipo D
endmodule

module Multiplexador_8x1 (
  input  S2,
  input  S1,
  input  S0,
  input  I0,
  input  I1,
  input  I2,
  input  I3,
  input  I4,
  input  I5,
  input  I6,
  input  I7,
  output S
);

  wire and_1_out, and_2_out, and_3_out, and_4_out, and_5_out, and_6_out, and_7_out, and_8_out, not_1_out,
       not_2_out, not_3_out, not_4_out, not_5_out, not_6_out, not_7_out, not_8_out, not_9_out, not_10_out,
       not_11_out, not_12_out;

  not not_1 (not_1_out, S2);
  not not_2 (not_2_out, S1);
  not not_3 (not_3_out, S0);
  not not_4 (not_4_out, S2);
  not not_5 (not_5_out, S1);
  not not_6 (not_6_out, S2);
  not not_7 (not_7_out, S0);
  not not_8 (not_8_out, S2);
  not not_9 (not_9_out, S1);
  not not_10 (not_10_out, S0);
  not not_11 (not_11_out, S1);
  not not_12 (not_12_out, S0);
  and and_1 (and_1_out, I0, not_1_out, not_2_out, not_3_out);
  and and_2 (and_2_out, I1, not_4_out, not_5_out, S0);
  and and_3 (and_3_out, I2, not_6_out, S1, not_7_out);
  and and_4 (and_4_out, I3, not_8_out, S1, S0);
  and and_5 (and_5_out, I4, S2, not_9_out, not_10_out);
  and and_6 (and_6_out, I5, S2, not_11_out, S0);
  and and_7 (and_7_out, I6, S2, S1, not_12_out);
  and and_8 (and_8_out, I7, S2, S1, S0);
  or or_1 (S, and_1_out, and_2_out, and_3_out, and_4_out, and_5_out, and_6_out, and_7_out, and_8_out);

  // Notes on the sheet:
  //   Multiplexador 8x1
endmodule

module Registrador_de_8_bits (
  input  [7:0] I,
  input  CLK,
  output [7:0] S
);

  wire flip_flop_tipo_d_7_q_prime;

  Flip_flop_tipo_D flip_flop_tipo_d_1 (.D(I[7]), .Q(S[7]), .CLK(CLK));  // open: Q_prime
  Flip_flop_tipo_D flip_flop_tipo_d_2 (.D(I[6]), .Q(S[6]), .CLK(CLK));  // open: Q_prime
  Flip_flop_tipo_D flip_flop_tipo_d_3 (.D(I[5]), .Q(S[5]), .CLK(CLK));  // open: Q_prime
  Flip_flop_tipo_D flip_flop_tipo_d_4 (.D(I[4]), .Q(S[4]), .CLK(CLK));  // open: Q_prime
  Flip_flop_tipo_D flip_flop_tipo_d_5 (.D(I[3]), .Q(S[3]), .CLK(CLK));  // open: Q_prime
  Flip_flop_tipo_D flip_flop_tipo_d_6 (.D(I[2]), .Q(S[2]), .CLK(CLK));  // open: Q_prime
  Flip_flop_tipo_D flip_flop_tipo_d_7 (.D(I[1]), .Q(S[1]), .Q_prime(flip_flop_tipo_d_7_q_prime), .CLK(CLK));
  Flip_flop_tipo_D flip_flop_tipo_d_8 (.D(I[0]), .Q(S[0]), .CLK(CLK));  // open: Q_prime

  // Notes on the sheet:
  //   Registrador de 8 bits
endmodule

module Multiplexador_2X1_1_bit (
  input  in_1,
  input  in_2,
  input  in_3,
  output out_4
);

  wire and_1_out, and_2_out;

  and and_1 (and_1_out, in_1, ~in_3);  // AND_Gate
  and and_2 (and_2_out, in_2, in_3);
  or or_1 (out_4, and_1_out, and_2_out);
endmodule

module Multiplexador_2x1_8_bits (
  input  [7:0] entrada,
  input  [7:0] entrada_2,
  input  Chave,
  output [7:0] out_4
);

  Multiplexador_2X1_1_bit multiplexador_2x1_1_bit_1 (
    .in_1(entrada[0]), .in_2(entrada_2[0]), .in_3(Chave), .out_4(out_4[0]));
  Multiplexador_2X1_1_bit multiplexador_2x1_1_bit_2 (
    .in_1(entrada[1]), .in_2(entrada_2[1]), .in_3(Chave), .out_4(out_4[1]));
  Multiplexador_2X1_1_bit multiplexador_2x1_1_bit_3 (
    .in_1(entrada[2]), .in_2(entrada_2[2]), .in_3(Chave), .out_4(out_4[2]));
  Multiplexador_2X1_1_bit multiplexador_2x1_1_bit_4 (
    .in_1(entrada[3]), .in_2(entrada_2[3]), .in_3(Chave), .out_4(out_4[3]));
  Multiplexador_2X1_1_bit multiplexador_2x1_1_bit_5 (
    .in_1(entrada[4]), .in_2(entrada_2[4]), .in_3(Chave), .out_4(out_4[4]));
  Multiplexador_2X1_1_bit multiplexador_2x1_1_bit_6 (
    .in_1(entrada[5]), .in_2(entrada_2[5]), .in_3(Chave), .out_4(out_4[5]));
  Multiplexador_2X1_1_bit multiplexador_2x1_1_bit_7 (
    .in_1(entrada[6]), .in_2(entrada_2[6]), .in_3(Chave), .out_4(out_4[6]));
  Multiplexador_2X1_1_bit multiplexador_2x1_1_bit_8 (
    .in_1(entrada[7]), .in_2(entrada_2[7]), .in_3(Chave), .out_4(out_4[7]));
endmodule

module Multiplexador_8x1_8_bits (
  input  [7:0] in0,
  input  [7:0] in1,
  input  [7:0] in2,
  input  [7:0] in4,
  input  [7:0] in4_2,
  input  [7:0] in5,
  input  [7:0] in6,
  input  [7:0] in7,
  input  S,
  input  [2:0] chave,
  output [7:0] saida
);

  wire and_1_out, and_2_out, and_3_out;
  wire [7:0] multiplexador_2x1_8_bits_1_out_4, multiplexador_2x1_8_bits_2_out_4,
       multiplexador_2x1_8_bits_3_out_4, multiplexador_2x1_8_bits_4_out_4, multiplexador_2x1_8_bits_5_out_4,
       multiplexador_2x1_8_bits_6_out_4;

  Multiplexador_2x1_8_bits multiplexador_2x1_8_bits_1 (
    .entrada(in0), .entrada_2(in1), .out_4(multiplexador_2x1_8_bits_1_out_4), .Chave(and_2_out));
  Multiplexador_2x1_8_bits multiplexador_2x1_8_bits_2 (
    .entrada(in2), .entrada_2(in4), .out_4(multiplexador_2x1_8_bits_2_out_4), .Chave(and_2_out));
  Multiplexador_2x1_8_bits multiplexador_2x1_8_bits_3 (
    .entrada(in4_2), .entrada_2(in5), .out_4(multiplexador_2x1_8_bits_3_out_4), .Chave(and_2_out));
  Multiplexador_2x1_8_bits multiplexador_2x1_8_bits_4 (
    .entrada(in6), .entrada_2(in7), .out_4(multiplexador_2x1_8_bits_4_out_4), .Chave(and_2_out));
  and and_1 (and_1_out, chave[1], S);
  and and_2 (and_2_out, chave[0], S);
  Multiplexador_2x1_8_bits multiplexador_2x1_8_bits_5 (
    .entrada(multiplexador_2x1_8_bits_1_out_4), .entrada_2(multiplexador_2x1_8_bits_2_out_4),
    .out_4(multiplexador_2x1_8_bits_5_out_4), .Chave(and_1_out));
  Multiplexador_2x1_8_bits multiplexador_2x1_8_bits_6 (
    .entrada(multiplexador_2x1_8_bits_3_out_4), .entrada_2(multiplexador_2x1_8_bits_4_out_4),
    .out_4(multiplexador_2x1_8_bits_6_out_4), .Chave(and_1_out));
  and and_3 (and_3_out, chave[2], S);
  Multiplexador_2x1_8_bits multiplexador_2x1_8_bits_7 (
    .entrada(multiplexador_2x1_8_bits_5_out_4), .entrada_2(multiplexador_2x1_8_bits_6_out_4), .out_4(saida),
    .Chave(and_3_out));
endmodule
