// Logisim project 7.banco_de_registradores.circ as structural Verilog
module registrador (
  input  [7:0] entrada,
  input  CLOCK,
  output [7:0] \saída 
);

  flipflop_D flipflop_d_1 (.D(entrada[0]), .CLK(CLOCK), .out_3(\saída [0]));  // open: out_4
  flipflop_D flipflop_d_2 (.D(entrada[1]), .CLK(CLOCK), .out_3(\saída [1]));  // open: out_4
  flipflop_D flipflop_d_3 (.D(entrada[2]), .CLK(CLOCK), .out_3(\saída [2]));  // open: out_4
  flipflop_D flipflop_d_4 (.D(entrada[3]), .CLK(CLOCK), .out_3(\saída [3]));  // open: out_4
  flipflop_D flipflop_d_5 (.D(entrada[4]), .CLK(CLOCK), .out_3(\saída [4]));  // open: out_4
  flipflop_D flipflop_d_6 (.D(entrada[5]), .CLK(CLOCK), .out_3(\saída [5]));  // open: out_4
  flipflop_D flipflop_d_7 (.D(entrada[6]), .CLK(CLOCK), .out_3(\saída [6]));  // open: out_4
  flipflop_D flipflop_d_8 (.D(entrada[7]), .CLK(CLOCK), .out_3(\saída [7]));  // open: out_4
endmodule

module bando_registrador_8bits (
  input  [3:0] RX_select,
  input  LEITURA,
  input  [7:0] data_in,
  input  [3:0] Ry_select,
  input  Write,
  input  [3:0] Write_select,
  output [7:0] Rx,
  output [7:0] Ry
);

  wire demux_1x16_1_bit_1_s0, demux_1x16_1_bit_1_s1, demux_1x16_1_bit_1_s2, demux_1x16_1_bit_1_s3,
       demux_1x16_1_bit_1_s4, demux_1x16_1_bit_1_s5, demux_1x16_1_bit_1_s6, demux_1x16_1_bit_1_s7,
       demux_1x16_1_bit_1_s8, demux_1x16_1_bit_1_s9, demux_1x16_1_bit_1_s10, demux_1x16_1_bit_1_s11,
       demux_1x16_1_bit_1_s12, demux_1x16_1_bit_1_s13, demux_1x16_1_bit_1_s14, demux_1x16_1_bit_1_s15;
  wire [7:0] \registrador_1_saída , \registrador_2_saída , \registrador_3_saída , \registrador_4_saída ,
       \registrador_5_saída , \registrador_6_saída , \registrador_7_saída , \registrador_8_saída ,
       \registrador_9_saída , \registrador_10_saída , \registrador_11_saída , \registrador_12_saída ,
       \registrador_13_saída , \registrador_14_saída , \registrador_15_saída , \registrador_16_saída ;

  DEMUX_1x16_1_bit demux_1x16_1_bit_1 (
    .KEY(Write_select), .l(Write), .S0(demux_1x16_1_bit_1_s0), .S1(demux_1x16_1_bit_1_s1),
    .S2(demux_1x16_1_bit_1_s2), .S3(demux_1x16_1_bit_1_s3), .S4(demux_1x16_1_bit_1_s4),
    .S5(demux_1x16_1_bit_1_s5), .S6(demux_1x16_1_bit_1_s6), .S7(demux_1x16_1_bit_1_s7),
    .S8(demux_1x16_1_bit_1_s8), .S9(demux_1x16_1_bit_1_s9), .S10(demux_1x16_1_bit_1_s10),
    .S11(demux_1x16_1_bit_1_s11), .S12(demux_1x16_1_bit_1_s12), .S13(demux_1x16_1_bit_1_s13),
    .S14(demux_1x16_1_bit_1_s14), .S15(demux_1x16_1_bit_1_s15));
  registrador registrador_1 (.entrada(data_in), .CLOCK(demux_1x16_1_bit_1_s0), .\saída (\registrador_1_saída ));
  registrador registrador_2 (.entrada(data_in), .CLOCK(demux_1x16_1_bit_1_s1), .\saída (\registrador_2_saída ));
  registrador registrador_3 (.entrada(data_in), .CLOCK(demux_1x16_1_bit_1_s2), .\saída (\registrador_3_saída ));
  registrador registrador_4 (.entrada(data_in), .CLOCK(demux_1x16_1_bit_1_s3), .\saída (\registrador_4_saída ));
  registrador registrador_5 (.entrada(data_in), .CLOCK(demux_1x16_1_bit_1_s4), .\saída (\registrador_5_saída ));
  registrador registrador_6 (.entrada(data_in), .CLOCK(demux_1x16_1_bit_1_s5), .\saída (\registrador_6_saída ));
  registrador registrador_7 (.entrada(data_in), .CLOCK(demux_1x16_1_bit_1_s6), .\saída (\registrador_7_saída ));
  registrador registrador_8 (.entrada(data_in), .CLOCK(demux_1x16_1_bit_1_s7), .\saída (\registrador_8_saída ));
  registrador registrador_9 (.entrada(data_in), .CLOCK(demux_1x16_1_bit_1_s8), .\saída (\registrador_9_saída ));
  registrador registrador_10 (.entrada(data_in), .CLOCK(demux_1x16_1_bit_1_s9), .\saída (\registrador_10_saída ));
  registrador registrador_11 (.entrada(data_in), .CLOCK(demux_1x16_1_bit_1_s10), .\saída (\registrador_11_saída ));
  registrador registrador_12 (.entrada(data_in), .CLOCK(demux_1x16_1_bit_1_s11), .\saída (\registrador_12_saída ));
  registrador registrador_13 (.entrada(data_in), .CLOCK(demux_1x16_1_bit_1_s12), .\saída (\registrador_13_saída ));
  registrador registrador_14 (.entrada(data_in), .CLOCK(demux_1x16_1_bit_1_s13), .\saída (\registrador_14_saída ));
  registrador registrador_15 (.entrada(data_in), .CLOCK(demux_1x16_1_bit_1_s14), .\saída (\registrador_15_saída ));
  registrador registrador_16 (.entrada(data_in), .CLOCK(demux_1x16_1_bit_1_s15), .\saída (\registrador_16_saída ));
  MUX_16X1_8bits mux_16x1_8bits_1 (
    .in0(\registrador_1_saída ), .in1(\registrador_2_saída ), .in2(\registrador_3_saída ),
    .in3(\registrador_4_saída ), .in4(\registrador_5_saída ), .in5(\registrador_6_saída ),
    .in6(\registrador_7_saída ), .in7(\registrador_8_saída ), .in8(\registrador_9_saída ),
    .in9(\registrador_10_saída ), .in10(\registrador_11_saída ), .in11(\registrador_12_saída ),
    .in12(\registrador_13_saída ), .in13(\registrador_14_saída ), .in14(\registrador_15_saída ),
    .in15(\registrador_16_saída ), .CHAVE(RX_select), .\SAÍDA (Rx), .S(LEITURA));
  MUX_16X1_8bits mux_16x1_8bits_2 (
    .in0(\registrador_1_saída ), .in1(\registrador_2_saída ), .in2(\registrador_3_saída ),
    .in3(\registrador_4_saída ), .in4(\registrador_5_saída ), .in5(\registrador_6_saída ),
    .in6(\registrador_7_saída ), .in7(\registrador_8_saída ), .in8(\registrador_9_saída ),
    .in9(\registrador_10_saída ), .in10(\registrador_11_saída ), .in11(\registrador_12_saída ),
    .in12(\registrador_13_saída ), .in13(\registrador_14_saída ), .in14(\registrador_15_saída ),
    .in15(\registrador_16_saída ), .CHAVE(Ry_select), .\SAÍDA (Ry), .S(LEITURA));
endmodule

module flipflop_D (
  input  D,
  input  CLK,
  output out_3,
  output out_4
);

  wire nand_1_out, nand_2_out, not_1_out;

  not not_1 (not_1_out, D);
  nand nand_1 (nand_1_out, D, CLK);
  nand nand_2 (nand_2_out, not_1_out, CLK);
  nand nand_3 (out_3, nand_1_out, out_4);
  nand nand_4 (out_4, out_3, nand_2_out);
endmodule

module DEMUX_1x16_1_bit (
  input  [3:0] KEY,
  input  l,
  output S0,
  output S1,
  output S2,
  output S3,
  output S4,
  output S5,
  output S6,
  output S7,
  output S8,
  output S9,
  output S10,
  output S11,
  output S12,
  output S13,
  output S14,
  output S15
);

  wire not_1_out, not_2_out, not_3_out, not_4_out;

  not not_1 (not_1_out, KEY[0]);
  not not_2 (not_2_out, KEY[1]);
  not not_3 (not_3_out, KEY[2]);
  not not_4 (not_4_out, KEY[3]);
  and and_1 (S0, l, not_1_out, not_2_out, not_3_out, not_4_out);
  and and_2 (S1, l, KEY[0], not_2_out, not_3_out, not_4_out);
  and and_3 (S2, l, not_1_out, KEY[1], not_3_out, not_4_out);
  and and_4 (S3, l, KEY[0], KEY[1], not_3_out, not_4_out);
  and and_5 (S4, l, not_1_out, not_2_out, KEY[2], not_4_out);
  and and_6 (S5, l, KEY[0], not_2_out, KEY[2], not_4_out);
  and and_7 (S6, l, not_1_out, KEY[1], KEY[2], not_4_out);
  and and_8 (S7, l, KEY[0], KEY[1], KEY[2], not_4_out);
  and and_9 (S8, l, not_1_out, not_2_out, not_3_out, KEY[3]);
  and and_10 (S9, l, KEY[0], not_2_out, not_3_out, KEY[3]);
  and and_11 (S10, l, not_1_out, KEY[1], not_3_out, KEY[3]);
  and and_12 (S11, l, KEY[0], KEY[1], not_3_out, KEY[3]);
  and and_13 (S12, l, not_1_out, not_2_out, KEY[2], KEY[3]);
  and and_14 (S13, l, KEY[0], not_2_out, KEY[2], KEY[3]);
  and and_15 (S14, l, not_1_out, KEY[1], KEY[2], KEY[3]);
  and and_16 (S15, l, KEY[0], KEY[1], KEY[2], KEY[3]);
endmodule

module MUX_2X1bit (
  input  in_1,
  input  in_2,
  input  in_3,
  output out_4
);

  wire and_1_out, and_2_out, not_1_out;

  not not_1 (not_1_out, in_3);
  and and_1 (and_1_out, in_1, not_1_out);
  and and_2 (and_2_out, in_2, in_3);
  or or_1 (out_4, and_1_out, and_2_out);
endmodule

module MUX_2X1_8bits (
  input  [7:0] entrada,
  input  chave,
  input  [7:0] entrada_2,
  output [7:0] out_4
);

  MUX_2X1bit mux_2x1bit_1 (.in_1(entrada[0]), .in_2(entrada_2[0]), .in_3(chave), .out_4(out_4[0]));
  MUX_2X1bit mux_2x1bit_2 (.in_1(entrada[1]), .in_2(entrada_2[1]), .in_3(chave), .out_4(out_4[1]));
  MUX_2X1bit mux_2x1bit_3 (.in_1(entrada[2]), .in_2(entrada_2[2]), .in_3(chave), .out_4(out_4[2]));
  MUX_2X1bit mux_2x1bit_4 (.in_1(entrada[3]), .in_2(entrada_2[3]), .in_3(chave), .out_4(out_4[3]));
  MUX_2X1bit mux_2x1bit_5 (.in_1(entrada[4]), .in_2(entrada_2[4]), .in_3(chave), .out_4(out_4[4]));
  MUX_2X1bit mux_2x1bit_6 (.in_1(entrada[5]), .in_2(entrada_2[5]), .in_3(chave), .out_4(out_4[5]));
  MUX_2X1bit mux_2x1bit_7 (.in_1(entrada[6]), .in_2(entrada_2[6]), .in_3(chave), .out_4(out_4[6]));
  MUX_2X1bit mux_2x1bit_8 (.in_1(entrada[7]), .in_2(entrada_2[7]), .in_3(chave), .out_4(out_4[7]));
endmodule

module MUX_8x1_8_bits (
  input  [7:0] in0,
  input  [7:0] in1,
  input  [7:0] in2,
  input  [7:0] in3,
  input  [7:0] in4,
  input  [7:0] in5,
  input  [7:0] in6,
  input  [7:0] in7,
  input  S,
  input  [2:0] chave,
  output [7:0] \saída 
);

  wire and_1_out, and_2_out, and_3_out;
  wire [7:0] mux_2x1_8bits_1_out_4, mux_2x1_8bits_2_out_4, mux_2x1_8bits_3_out_4, mux_2x1_8bits_4_out_4,
       mux_2x1_8bits_5_out_4, mux_2x1_8bits_6_out_4;

  MUX_2X1_8bits mux_2x1_8bits_1 (.entrada(in0), .entrada_2(in1), .out_4(mux_2x1_8bits_1_out_4), .chave(and_1_out));
  MUX_2X1_8bits mux_2x1_8bits_2 (.entrada(in2), .entrada_2(in3), .out_4(mux_2x1_8bits_2_out_4), .chave(and_1_out));
  MUX_2X1_8bits mux_2x1_8bits_3 (.entrada(in4), .entrada_2(in5), .out_4(mux_2x1_8bits_3_out_4), .chave(and_1_out));
  MUX_2X1_8bits mux_2x1_8bits_4 (.entrada(in6), .entrada_2(in7), .out_4(mux_2x1_8bits_4_out_4), .chave(and_1_out));
  and and_1 (and_1_out, chave[0], S);
  and and_2 (and_2_out, chave[1], S);
  MUX_2X1_8bits mux_2x1_8bits_5 (
    .entrada(mux_2x1_8bits_1_out_4), .entrada_2(mux_2x1_8bits_2_out_4), .out_4(mux_2x1_8bits_5_out_4),
    .chave(and_2_out));
  MUX_2X1_8bits mux_2x1_8bits_6 (
    .entrada(mux_2x1_8bits_3_out_4), .entrada_2(mux_2x1_8bits_4_out_4), .out_4(mux_2x1_8bits_6_out_4),
    .chave(and_2_out));
  MUX_2X1_8bits mux_2x1_8bits_7 (
    .entrada(mux_2x1_8bits_5_out_4), .entrada_2(mux_2x1_8bits_6_out_4), .out_4(\saída ), .chave(and_3_out));
  and and_3 (and_3_out, chave[2], S);
endmodule

module MUX_16X1_8bits (
  input  [7:0] in0,
  input  [7:0] in1,
  input  [7:0] in2,
  input  [7:0] in3,
  input  [7:0] in4,
  input  [7:0] in5,
  input  [7:0] in6,
  input  [7:0] in7,
  input  [7:0] in8,
  input  [7:0] in9,
  input  [7:0] in10,
  input  [7:0] in11,
  input  [7:0] in12,
  input  [7:0] in13,
  input  [7:0] in14,
  input  [7:0] in15,
  input  S,
  input  [3:0] CHAVE,
  output [7:0] \SAÍDA 
);

  wire and_1_out, and_2_out, and_3_out, and_4_out;
  wire [7:0] mux_2x1_8bits_1_out_4, mux_2x1_8bits_2_out_4, mux_2x1_8bits_3_out_4, mux_2x1_8bits_4_out_4,
       mux_2x1_8bits_5_out_4, mux_2x1_8bits_6_out_4, mux_2x1_8bits_7_out_4, mux_2x1_8bits_8_out_4,
       mux_2x1_8bits_9_out_4, mux_2x1_8bits_10_out_4, mux_2x1_8bits_11_out_4, mux_2x1_8bits_12_out_4,
       mux_2x1_8bits_13_out_4, mux_2x1_8bits_15_out_4;

  MUX_2X1_8bits mux_2x1_8bits_1 (.entrada(in0), .entrada_2(in1), .out_4(mux_2x1_8bits_1_out_4), .chave(and_1_out));
  MUX_2X1_8bits mux_2x1_8bits_2 (.entrada(in2), .entrada_2(in3), .out_4(mux_2x1_8bits_2_out_4), .chave(and_1_out));
  MUX_2X1_8bits mux_2x1_8bits_3 (.entrada(in4), .entrada_2(in5), .out_4(mux_2x1_8bits_3_out_4), .chave(and_1_out));
  MUX_2X1_8bits mux_2x1_8bits_4 (.entrada(in6), .entrada_2(in7), .out_4(mux_2x1_8bits_4_out_4), .chave(and_1_out));
  MUX_2X1_8bits mux_2x1_8bits_5 (.entrada(in8), .entrada_2(in9), .out_4(mux_2x1_8bits_5_out_4), .chave(and_1_out));
  MUX_2X1_8bits mux_2x1_8bits_6 (.entrada(in10), .entrada_2(in11), .out_4(mux_2x1_8bits_6_out_4), .chave(and_1_out));
  MUX_2X1_8bits mux_2x1_8bits_7 (.entrada(in12), .entrada_2(in13), .out_4(mux_2x1_8bits_7_out_4), .chave(and_1_out));
  MUX_2X1_8bits mux_2x1_8bits_8 (.entrada(in14), .entrada_2(in15), .out_4(mux_2x1_8bits_8_out_4), .chave(and_1_out));
  and and_1 (and_1_out, CHAVE[0], S);
  MUX_2X1_8bits mux_2x1_8bits_9 (
    .entrada(mux_2x1_8bits_1_out_4), .entrada_2(mux_2x1_8bits_2_out_4), .out_4(mux_2x1_8bits_9_out_4),
    .chave(and_2_out));
  MUX_2X1_8bits mux_2x1_8bits_10 (
    .entrada(mux_2x1_8bits_3_out_4), .entrada_2(mux_2x1_8bits_4_out_4), .out_4(mux_2x1_8bits_10_out_4),
    .chave(and_2_out));
  MUX_2X1_8bits mux_2x1_8bits_11 (
    .entrada(mux_2x1_8bits_5_out_4), .entrada_2(mux_2x1_8bits_6_out_4), .out_4(mux_2x1_8bits_11_out_4),
    .chave(and_2_out));
  MUX_2X1_8bits mux_2x1_8bits_12 (
    .entrada(mux_2x1_8bits_7_out_4), .entrada_2(mux_2x1_8bits_8_out_4), .out_4(mux_2x1_8bits_12_out_4),
    .chave(and_2_out));
  and and_2 (and_2_out, CHAVE[1], S);
  and and_3 (and_3_out, CHAVE[2], S);
  MUX_2X1_8bits mux_2x1_8bits_13 (
    .entrada(mux_2x1_8bits_9_out_4), .entrada_2(mux_2x1_8bits_10_out_4), .out_4(mux_2x1_8bits_13_out_4),
    .chave(and_3_out));
  MUX_2X1_8bits mux_2x1_8bits_14 (
    .entrada(mux_2x1_8bits_13_out_4), .entrada_2(mux_2x1_8bits_15_out_4), .out_4(\SAÍDA ), .chave(and_4_out));
  MUX_2X1_8bits mux_2x1_8bits_15 (
    .entrada(mux_2x1_8bits_11_out_4), .entrada_2(mux_2x1_8bits_12_out_4), .out_4(mux_2x1_8bits_15_out_4),
    .chave(and_3_out));
  and and_4 (and_4_out, CHAVE[3], S);
endmodule
