// Logisim project banco_de_registradores.circ as structural Verilog
module registrador (
  input  CLOCK,
  input  [7:0] entrada,
  output [7:0] \saída 
);

  D_Flip_Flop d_ff_1 (.clk(CLOCK), .D(entrada[0]), .Q(\saída [0]));  // open: Qn, preset, en, reset
  D_Flip_Flop d_ff_2 (.clk(CLOCK), .D(entrada[1]), .Q(\saída [1]));  // open: Qn, preset, en, reset
  D_Flip_Flop d_ff_3 (.clk(CLOCK), .D(entrada[2]), .Q(\saída [2]));  // open: Qn, preset, en, reset
  D_Flip_Flop d_ff_4 (.clk(CLOCK), .D(entrada[3]), .Q(\saída [3]));  // open: Qn, preset, en, reset
  D_Flip_Flop d_ff_5 (.clk(CLOCK), .D(entrada[4]), .Q(\saída [4]));  // open: Qn, preset, en, reset
  D_Flip_Flop d_ff_6 (.clk(CLOCK), .D(entrada[5]), .Q(\saída [5]));  // open: Qn, preset, en, reset
  D_Flip_Flop d_ff_7 (.clk(CLOCK), .D(entrada[6]), .Q(\saída [6]));  // open: Qn, preset, en, reset
  D_Flip_Flop d_ff_8 (.clk(CLOCK), .D(entrada[7]), .Q(\saída [7]));  // open: Qn, preset, en, reset
endmodule

module bando_registrador_8bits (
  input  [3:0] in_1,
  input  [7:0] in_2,
  input  in_3,
  input  [3:0] in_4,
  output [7:0] out_5
);

  wire demultiplexer_1_out0, demultiplexer_1_out1, demultiplexer_1_out2, demultiplexer_1_out3,
       demultiplexer_1_out4, demultiplexer_1_out5, demultiplexer_1_out6, demultiplexer_1_out7,
       demultiplexer_1_out8, demultiplexer_1_out9, demultiplexer_1_out10, demultiplexer_1_out11,
       demultiplexer_1_out12, demultiplexer_1_out13, demultiplexer_1_out14, demultiplexer_1_out15;
  wire [7:0] \registrador_1_saída , \registrador_2_saída , \registrador_3_saída , \registrador_4_saída ,
       \registrador_5_saída , \registrador_6_saída , \registrador_7_saída , \registrador_8_saída ,
       \registrador_9_saída , \registrador_10_saída , \registrador_11_saída , \registrador_12_saída ,
       \registrador_13_saída , \registrador_14_saída , \registrador_15_saída , \registrador_16_saída ;

  Demultiplexer #(.select(4)) demultiplexer_1 (
    .out0(demultiplexer_1_out0), .out1(demultiplexer_1_out1), .out2(demultiplexer_1_out2),
    .out3(demultiplexer_1_out3), .out4(demultiplexer_1_out4), .out5(demultiplexer_1_out5),
    .out6(demultiplexer_1_out6), .out7(demultiplexer_1_out7), .out8(demultiplexer_1_out8),
    .out9(demultiplexer_1_out9), .out10(demultiplexer_1_out10), .out11(demultiplexer_1_out11),
    .out12(demultiplexer_1_out12), .out13(demultiplexer_1_out13), .out14(demultiplexer_1_out14),
    .out15(demultiplexer_1_out15), .in(in_3), .sel(in_4));  // open: en
  registrador registrador_1 (.CLOCK(demultiplexer_1_out0), .entrada(in_2), .\saída (\registrador_1_saída ));
  registrador registrador_2 (.CLOCK(demultiplexer_1_out1), .entrada(in_2), .\saída (\registrador_2_saída ));
  registrador registrador_3 (.CLOCK(demultiplexer_1_out2), .entrada(in_2), .\saída (\registrador_3_saída ));
  registrador registrador_4 (.CLOCK(demultiplexer_1_out3), .entrada(in_2), .\saída (\registrador_4_saída ));
  registrador registrador_5 (.CLOCK(demultiplexer_1_out4), .entrada(in_2), .\saída (\registrador_5_saída ));
  registrador registrador_6 (.CLOCK(demultiplexer_1_out5), .entrada(in_2), .\saída (\registrador_6_saída ));
  registrador registrador_7 (.CLOCK(demultiplexer_1_out6), .entrada(in_2), .\saída (\registrador_7_saída ));
  registrador registrador_8 (.CLOCK(demultiplexer_1_out7), .entrada(in_2), .\saída (\registrador_8_saída ));
  registrador registrador_9 (.CLOCK(demultiplexer_1_out8), .entrada(in_2), .\saída (\registrador_9_saída ));
  registrador registrador_10 (.CLOCK(demultiplexer_1_out9), .entrada(in_2), .\saída (\registrador_10_saída ));
  registrador registrador_11 (.CLOCK(demultiplexer_1_out10), .entrada(in_2), .\saída (\registrador_11_saída ));
  registrador registrador_12 (.CLOCK(demultiplexer_1_out11), .entrada(in_2), .\saída (\registrador_12_saída ));
  registrador registrador_13 (.CLOCK(demultiplexer_1_out12), .entrada(in_2), .\saída (\registrador_13_saída ));
  registrador registrador_14 (.CLOCK(demultiplexer_1_out13), .\saída (\registrador_14_saída ));  // open: entrada
  registrador registrador_15 (.CLOCK(demultiplexer_1_out14), .entrada(in_2), .\saída (\registrador_15_saída ));
  registrador registrador_16 (.CLOCK(demultiplexer_1_out15), .entrada(in_2), .\saída (\registrador_16_saída ));
  Multiplexer #(.select(4), .width(8)) multiplexer_1 (
    .in0(\registrador_1_saída ), .in1(\registrador_2_saída ), .in2(\registrador_3_saída ),
    .in3(\registrador_4_saída ), .in4(\registrador_5_saída ), .in5(\registrador_6_saída ),
    .in6(\registrador_7_saída ), .in7(\registrador_8_saída ), .in8(\registrador_9_saída ),
    .in9(\registrador_10_saída ), .in10(\registrador_11_saída ), .in11(\registrador_12_saída ),
    .in12(\registrador_13_saída ), .in13(\registrador_14_saída ), .in14(\registrador_15_saída ),
    .in15(\registrador_16_saída ), .out(out_5), .sel(in_1));  // open: en
endmodule
