// Logisim project 8. Somador 8 bits.circ as structural Verilog: 3 circuits, main circuit Porta XOR
// XOR
module Porta_XOR (
  input  A,
  input  B,
  output S
);

  wire and_1_out, and_2_out, not_1_out, not_2_out;

  not not_1 (not_1_out, A);
  not not_2 (not_2_out, B);
  and and_1 (and_1_out, not_1_out, B);
  and and_2 (and_2_out, A, not_2_out);
  or or_1 (S, and_1_out, and_2_out);

  // Notes on the sheet:
  //   PORTA XOR
endmodule

// 1 bit
module Somador_de_1_bit (
  input  A,
  input  B,
  input  cin,
  output S,
  output cout
);

  wire and_1_out, and_2_out, and_3_out, porta_xor_1_s;

  Porta_XOR porta_xor_1 (.A(A), .B(B), .S(porta_xor_1_s));
  Porta_XOR porta_xor_2 (.A(porta_xor_1_s), .B(cin), .S(S));
  and and_1 (and_1_out, A, B);
  and and_2 (and_2_out, A, B);
  and and_3 (and_3_out, B, B);
  or or_1 (cout, and_1_out, and_2_out, and_3_out);

  // Notes on the sheet:
  //   SOMADOR - 1 BIT
endmodule

module Somador_de_8_bits (
  input  [7:0] in_1,
  input  [7:0] in_2,
  output [7:0] SOMA,
  output out_4
);

  wire FULL_ADDER_2_cout, FULL_ADDER_3_cout, FULL_ADDER_4_cout, FULL_ADDER_5_cout, FULL_ADDER_6_cout,
       FULL_ADDER_7_cout, FULL_ADDER_cout;

  Somador_de_1_bit FULL_ADDER (.A(in_1[0]), .B(in_2[0]), .cin(1'b0), .S(SOMA[0]), .cout(FULL_ADDER_cout));
  Somador_de_1_bit FULL_ADDER_2 (
    .A(in_1[1]), .B(in_2[1]), .cin(FULL_ADDER_cout), .S(SOMA[1]), .cout(FULL_ADDER_2_cout));
  Somador_de_1_bit FULL_ADDER_3 (
    .A(in_1[2]), .B(in_2[2]), .cin(FULL_ADDER_2_cout), .S(SOMA[2]), .cout(FULL_ADDER_3_cout));
  Somador_de_1_bit FULL_ADDER_4 (
    .A(in_1[3]), .B(in_2[3]), .cin(FULL_ADDER_3_cout), .S(SOMA[3]), .cout(FULL_ADDER_4_cout));
  Somador_de_1_bit FULL_ADDER_5 (
    .A(in_1[4]), .B(in_2[4]), .cin(FULL_ADDER_4_cout), .S(SOMA[4]), .cout(FULL_ADDER_5_cout));
  Somador_de_1_bit FULL_ADDER_6 (
    .A(in_1[5]), .B(in_2[5]), .cin(FULL_ADDER_5_cout), .S(SOMA[5]), .cout(FULL_ADDER_6_cout));
  Somador_de_1_bit FULL_ADDER_7 (
    .A(in_1[6]), .B(in_2[6]), .cin(FULL_ADDER_6_cout), .S(SOMA[6]), .cout(FULL_ADDER_7_cout));
  Somador_de_1_bit FULL_ADDER_8 (.A(in_1[7]), .B(in_2[7]), .cin(FULL_ADDER_7_cout), .S(SOMA[7]), .cout(out_4));

  // Notes on the sheet:
  //   SOMADOR - 8 BITS
endmodule
