// Logisim project 9.Detectorbinário_'101'.circ as structural Verilog
module _9__Detector__101 (
  input  A,
  input  B,
  input  C,
  output out_4
);

  wire not_1_out;

  not not_1 (not_1_out, B);
  and and_1 (out_4, A, not_1_out, C);
endmodule
