// Logisim project 12. Máquiana de Estados.circ as structural Verilog: 2 circuits, main circuit Máquina de Estados
module \Máquina_de_Estados  (
  input  in_1,
  output out_2
);

  wire and_1_out, and_2_out, clock_1_out, or_1_out;

  and and_1 (and_1_out, ~out_2, in_1);  // AND_Gate
  buf and_2 (and_2_out, ~in_1);  // AND_Gate AND_Gate
  Clock clock_1 (.out(clock_1_out));
  or or_1 (or_1_out, and_1_out, and_2_out);
  D_Flip_Flop d_ff_1 (.clk(clock_1_out), .D(or_1_out), .Q(out_2));  // open: Qn, preset, en, reset
endmodule

// D
module Flip_flop_D (
  input  D,
  output Q,
  output Q_prime
);

  wire CLK_out, nand_1_out, nand_2_out, not_1_out;

  not not_1 (not_1_out, D);
  Clock CLK (.out(CLK_out));
  nand nand_1 (nand_1_out, D, CLK_out);
  nand nand_2 (nand_2_out, not_1_out, CLK_out);
  nand nand_3 (Q, nand_1_out, Q_prime);
  nand nand_4 (Q_prime, Q, nand_2_out);

  // Notes on the sheet:
  //   Flip-flop do tipo D
endmodule
