// Logisim project 13.contador_sincrono.circ as structural Verilog
module contador_sincrono (
  output [3:0] out_1
);

  wire and_1_out, and_2_out, clock_1_out, d_ff_1_qn, xor_1_out, xor_2_out, xor_3_out;

  Clock clock_1 (.out(clock_1_out));
  D_Flip_Flop d_ff_1 (.clk(clock_1_out), .D(d_ff_1_qn), .Q(out_1[0]), .Qn(d_ff_1_qn));  // open: preset, en, reset
  D_Flip_Flop d_ff_2 (.clk(clock_1_out), .D(xor_1_out), .Q(out_1[1]));  // open: Qn, preset, en, reset
  D_Flip_Flop d_ff_3 (.clk(clock_1_out), .D(xor_2_out), .Q(out_1[2]));  // open: Qn, preset, en, reset
  D_Flip_Flop d_ff_4 (.clk(clock_1_out), .D(xor_3_out), .Q(out_1[3]));  // open: Qn, preset, en, reset
  xor xor_1 (xor_1_out, out_1[0], out_1[1]);
  and and_1 (and_1_out, out_1[0], out_1[1]);
  xor xor_2 (xor_2_out, and_1_out, out_1[2]);
  and and_2 (and_2_out, out_1[0], out_1[1], out_1[2]);
  xor xor_3 (xor_3_out, and_2_out, out_1[3]);
  Hex_Digit_Display hex_digit_display_1 (.value(out_1));  // open: dp
endmodule
