// Logisim project 15.circuito_otimizado.circ as structural Verilog: 2 circuits, main circuit main
module main (
  input  in_1,
  input  in_2
);

  wire and_1_out, and_2_out, not_1_out, not_2_out, or_1_out;

  not not_1 (not_1_out, in_1);
  not not_2 (not_2_out, in_2);
  and and_1 (and_1_out, not_1_out, not_2_out);
  and and_2 (and_2_out, in_2, in_1);
  or or_1 (or_1_out, and_1_out, and_2_out);
endmodule

module \xnor  (
  input  A,
  input  B,
  output S,
  output out_4
);

  wire and_1_out, and_2_out, not_1_out, not_2_out;

  not not_1 (not_1_out, A);
  not not_2 (not_2_out, B);
  and and_1 (and_1_out, not_1_out, not_2_out);
  and and_2 (and_2_out, A, B);
  xnor xnor_1 (out_4, A, B);
  or or_1 (S, and_1_out, and_2_out);

  // Notes on the sheet:
  //   A'B'
  //   AB
  //   S = AB + A'B'
  //   S = AB + A'B'
endmodule
