// Logisim project otimizacao_mapas.circ as structural Verilog
module CIRCUITO_OTIMIZADO (
  input  [2:0] ABC,
  output out_2
);

  wire and_1_out, and_2_out, and_3_out;

  and and_1 (and_1_out, ABC[0], ABC[2]);
  and and_2 (and_2_out, ABC[0], ABC[1]);
  and and_3 (and_3_out, ABC[1], ABC[2]);
  or or_1 (out_2, and_1_out, and_2_out, and_3_out);

  // Notes on the sheet:
  //   S = AC + AB + BC
endmodule

module CIRCUITO_NAO_OTIMIZADO (
  input  [2:0] ABC,
  output out_2
);

  wire and_1_out, and_2_out, and_3_out, and_4_out, not_1_out, not_2_out, not_3_out;

  not not_1 (not_1_out, ABC[2]);
  not not_2 (not_2_out, ABC[1]);
  not not_3 (not_3_out, ABC[0]);
  and and_1 (and_1_out, not_1_out, ABC[1], ABC[0]);
  and and_2 (and_2_out, ABC[2], not_2_out, ABC[0]);
  and and_3 (and_3_out, ABC[2], ABC[1], not_3_out);
  and and_4 (and_4_out, ABC[2], ABC[1], ABC[0]);
  or or_1 (out_2, and_1_out, and_2_out, and_3_out, and_4_out);

  // Notes on the sheet:
  //   S = A'BC + AB'C + ABC' + ABC
endmodule
