// Logisim project 16. Decodificador de 7 Segmentos.circ as structural Verilog: 8 circuits, main circuit A
module A (
  input  [3:0] ENTRADA,
  output \SAÍDA_A 
);

  wire and_1_out, and_2_out, and_3_out, and_4_out, and_5_out, and_6_out;

  and and_1 (and_1_out, ~ENTRADA[2], ~ENTRADA[0]);  // AND_Gate
  and and_2 (and_2_out, ~ENTRADA[3], ENTRADA[1]);  // AND_Gate
  and and_3 (and_3_out, ~ENTRADA[3], ENTRADA[2], ENTRADA[0]);  // AND_Gate
  and and_4 (and_4_out, ENTRADA[2], ENTRADA[1]);
  and and_5 (and_5_out, ENTRADA[3], ~ENTRADA[0]);  // AND_Gate
  and and_6 (and_6_out, ENTRADA[3], ~ENTRADA[2], ~ENTRADA[1]);  // AND_Gate
  or or_1 (\SAÍDA_A , and_1_out, and_2_out, and_3_out, and_4_out, and_5_out, and_6_out);
endmodule

module B (
  input  [3:0] ENTRADA,
  output \SAÍDA_B 
);

  wire and_1_out, and_2_out, and_3_out, and_4_out, and_5_out;

  and and_1 (and_1_out, ENTRADA[3], ~ENTRADA[1], ENTRADA[0]);  // AND_Gate
  and and_2 (and_2_out, ~ENTRADA[2], ~ENTRADA[0]);  // AND_Gate
  and and_3 (and_3_out, ~ENTRADA[3], ~ENTRADA[1], ~ENTRADA[0]);  // AND_Gate
  and and_4 (and_4_out, ~ENTRADA[3], ENTRADA[1], ENTRADA[0]);  // AND_Gate
  and and_5 (and_5_out, ~ENTRADA[3], ~ENTRADA[2]);  // AND_Gate
  or or_1 (\SAÍDA_B , and_1_out, and_2_out, and_3_out, and_4_out, and_5_out);
endmodule

module C (
  input  [3:0] ENTRADA,
  output \SAÍDA_C 
);

  wire and_1_out, and_2_out, and_3_out, and_4_out, and_5_out;

  and and_1 (and_1_out, ~ENTRADA[1], ENTRADA[0]);  // AND_Gate
  and and_2 (and_2_out, ~ENTRADA[3], ENTRADA[2]);  // AND_Gate
  and and_3 (and_3_out, ENTRADA[3], ~ENTRADA[2]);  // AND_Gate
  and and_4 (and_4_out, ~ENTRADA[3], ~ENTRADA[1]);  // AND_Gate
  and and_5 (and_5_out, ~ENTRADA[3], ~ENTRADA[0]);  // AND_Gate
  or or_1 (\SAÍDA_C , and_1_out, and_2_out, and_3_out, and_4_out, and_5_out);
endmodule

module D (
  input  [3:0] ENTRADA,
  output \SAÍDA_D 
);

  wire and_1_out, and_2_out, and_3_out, and_4_out, and_5_out;

  and and_1 (and_1_out, ENTRADA[2], ~ENTRADA[1], ENTRADA[0]);  // AND_Gate
  and and_2 (and_2_out, ~ENTRADA[2], ENTRADA[1], ENTRADA[0]);  // AND_Gate
  and and_3 (and_3_out, ENTRADA[2], ENTRADA[1], ~ENTRADA[0]);  // AND_Gate
  and and_4 (and_4_out, ~ENTRADA[3], ~ENTRADA[1]);  // AND_Gate
  and and_5 (and_5_out, ~ENTRADA[3], ~ENTRADA[2], ~ENTRADA[0]);  // AND_Gate
  or or_1 (\SAÍDA_D , and_1_out, and_2_out, and_3_out, and_4_out, and_5_out);
endmodule

module E (
  input  [3:0] ENTRADA,
  output \SAÍDA_D 
);

  wire and_1_out, and_2_out, and_3_out, and_4_out;

  and and_1 (and_1_out, ~ENTRADA[2], ~ENTRADA[0]);  // AND_Gate
  and and_2 (and_2_out, ENTRADA[1], ~ENTRADA[0]);  // AND_Gate
  and and_3 (and_3_out, ENTRADA[3], ENTRADA[1]);
  and and_4 (and_4_out, ENTRADA[3], ENTRADA[2]);
  or or_1 (\SAÍDA_D , and_1_out, and_2_out, and_3_out, and_4_out);
endmodule

module F (
  input  [3:0] ENTRADA,
  output \SAÍDA_F 
);

  wire and_1_out, and_2_out, and_3_out, and_4_out, and_5_out;

  and and_1 (and_1_out, ~ENTRADA[1], ~ENTRADA[0]);  // AND_Gate
  and and_2 (and_2_out, ENTRADA[2], ~ENTRADA[0]);  // AND_Gate
  and and_3 (and_3_out, ~ENTRADA[3], ENTRADA[2], ~ENTRADA[1]);  // AND_Gate
  and and_4 (and_4_out, ENTRADA[3], ~ENTRADA[2]);  // AND_Gate
  and and_5 (and_5_out, ENTRADA[3], ENTRADA[1]);
  or or_1 (\SAÍDA_F , and_1_out, and_2_out, and_3_out, and_4_out, and_5_out);
endmodule

module G (
  input  [3:0] ENTRADA,
  output \SAÍDA_G 
);

  wire and_1_out, and_2_out, and_3_out, and_4_out, and_5_out;

  and and_1 (and_1_out, ~ENTRADA[2], ENTRADA[1]);  // AND_Gate
  and and_2 (and_2_out, ENTRADA[3], ~ENTRADA[2]);  // AND_Gate
  and and_3 (and_3_out, ENTRADA[3], ENTRADA[0]);
  and and_4 (and_4_out, ENTRADA[1], ~ENTRADA[0]);  // AND_Gate
  and and_5 (and_5_out, ~ENTRADA[3], ENTRADA[2], ~ENTRADA[1]);  // AND_Gate
  or or_1 (\SAÍDA_G , and_1_out, and_2_out, and_3_out, and_4_out, and_5_out);
endmodule

module DECODIFICADOR (
  input  [3:0] in_1
);

  wire \a_1_saída_a , \b_1_saída_b , \c_1_saída_c , \d_1_saída_d , \e_1_saída_d , \f_1_saída_f ,
       \g_1_saída_g ;

  A a_1 (.ENTRADA(in_1), .\SAÍDA_A (\a_1_saída_a ));
  B b_1 (.ENTRADA(in_1), .\SAÍDA_B (\b_1_saída_b ));
  C c_1 (.ENTRADA(in_1), .\SAÍDA_C (\c_1_saída_c ));
  D d_1 (.ENTRADA(in_1), .\SAÍDA_D (\d_1_saída_d ));
  E e_1 (.ENTRADA(in_1), .\SAÍDA_D (\e_1_saída_d ));
  F f_1 (.ENTRADA(in_1), .\SAÍDA_F (\f_1_saída_f ));
  G g_1 (.ENTRADA(in_1), .\SAÍDA_G (\g_1_saída_g ));
  _7_Segment_Display u_7_segment_display_1 (
    .g(\g_1_saída_g ), .f(\f_1_saída_f ), .a(\a_1_saída_a ), .b(\b_1_saída_b ), .e(\e_1_saída_d ),
    .d(\d_1_saída_d ), .c(\c_1_saída_c ));  // open: dp
endmodule
